# Fritzing sketch hund_komponenter (saved by Fritzing 0.9.6b)
breadboards: 1

parts:
  Raspberry_Pi1 = Raspberry Pi B rev2
  LED1 = LED - 3mm [color="Green (555nm)" current=0.030 package="3 mm [THT]"]
  LED2 = LED - 3mm [color="Green (555nm)" current=0.030 package="3 mm [THT]"]
  LED3 = LED - 3mm [color="Red (633nm)" current=0.030 package="3 mm [THT]"]
  R1 = Resistor [tolerance=±5% power=0.25 resistance=220 package=THT]
  R2 = Resistor [tolerance=±5% power=0.25 resistance=220 package=THT]
  R3 = Resistor [tolerance=±5% power=0.25 resistance=220 package=THT]
  S1 = Pushbutton [package="[THT]"]
  DHT1 = DHT11 Humitidy and Temperature Sensor
  FC-1 = Sound Sensor
  R4 = Resistor [tolerance=±5% resistance=220 package="0402 [SMD]"]

nets:
  3V3: Raspberry_Pi1.3V3, DHT1.VDD, FC-1.VCC, R4.Pin_0
  GND: Raspberry_Pi1.GND, LED1.cathode, LED2.cathode, LED3.cathode, S1.Pin_3, S1.Pin_4, DHT1.GND, FC-1.GND
  N1: Raspberry_Pi1.GPIO_23, R1.Pin_1
  N2: Raspberry_Pi1.GPIO_18, R3.Pin_1
  N3: Raspberry_Pi1.GPIO_27, FC-1.OUT
  N4: Raspberry_Pi1.GPIO_22, S1.Pin_1, S1.Pin_2
  N5: Raspberry_Pi1.GPIO_24, R2.Pin_0
  N6: Raspberry_Pi1.GPIO_25, DHT1.DATA, R4.Pin_1
  N7: LED1.anode, R2.Pin_1
  N8: LED2.anode, R1.Pin_0
  N9: LED3.anode, R3.Pin_0

custom parts:
  DHT11 Humitidy and Temperature Sensor: DHT11 Humidity and Temperature Sensor
